// Logisim project 8bit_computer_FINAL.circ as structural Verilog: 10 circuits, main circuit main
module main (
  input  OE,
  input  [3:0] in_2,
  input  LOAD,
  input  [7:0] test,
  input  RESET,
  input  OE_2,
  input  SUB,
  input  Cin,
  input  [2:0] Select,
  input  OE_PC,
  input  WE_MAR,
  input  OE_MAR,
  input  OE_RAM,
  input  WE_MBR,
  input  CE_COUNTER,
  input  INT_OE_MBR,
  input  WE_IR,
  input  OE_IR,
  input  WE_MAR_2,
  input  OE_MAR_2,
  input  OE_RAM_2,
  input  WE_MBR_2,
  input  INT_OE_MBR_2,
  input  Reg_A,
  input  Reg_B,
  input  OE_ALU,
  input  WE_OUT_REG,
  input  OE_IR_2,
  input  WE_MAR_3,
  input  OE_OUTPUT,
  input  WE_MBR_3,
  input  OE_MAR_3,
  input  OE_MBR,
  input  WE_RAM,
  input  OE_IR_3,
  input  WE_MAR_4,
  input  OE_reg_A,
  input  WE_MBR_4,
  input  OE_MAR_4,
  input  OE_MBR_2,
  input  WE_RAM_2,
  output COUNT_OE,
  output WE,
  output CE,
  output OE_3,
  output [3:0] COUNTER_DATA,
  output WE_2,
  output OE_4,
  output [3:0] MAR_Data,
  output WE_3,
  output [7:0] IR_DATA,
  output OE_5,
  output IntOE,
  output WE_4,
  output OE_6,
  output [7:0] MBR_Data,
  output WE_5,
  output [7:0] Reg_A_DATA,
  output WE_6,
  output [7:0] ALU_RESULT,
  output OE_7,
  output OE_8,
  output Cout,
  output [7:0] out_64,
  output WE_7,
  output [7:0] Reg_B_DATA
);

  wire and_1_out, CLK_out, comparator_1_eq, not_1_out;
  wire [3:0] controlled_buffer_1_out, Decoder_2_dout, Decoder_2_dout_2, Decoder_2_dout_3, Decoder_2_dout_5,
       Decoder_2_dout_6, Decoder_2_dout_7, Decoder_3_dout_2, Decoder_3_dout_3, Decoder_3_dout_4,
       Decoder_3_dout_5, Decoder_dout, IR_HALT_DATA, MAR_dout;
  wire [7:0] bit_extender_1_out, n8bit_register_1_dout, n8bit_register_3_dout;
  wire [15:0] Decoder_3_dout;
  wire [31:0] Decoder_4_dout;
  wire [31:4] Decoder_dout_2;
  wire [31:12] Decoder_2_dout_4;

  Clock CLK (.out(CLK_out));
  Comparator #(.width(4)) comparator_1 (.a(IR_HALT_DATA), .b(4'b0101), .eq(comparator_1_eq));  // open: gt, lt
  BitSelector #(.group(4)) bitselector_1 (.in(IR_DATA), .out(IR_HALT_DATA), .sel(1'b1));
  not not_1 (not_1_out, comparator_1_eq);
  and and_1 (and_1_out, not_1_out, CLK_out);
  Clock CLK_2 ();  // open: out
  _8bit_register u_8bit_register_1 (
    .CLOCK(and_1_out), .DOut(n8bit_register_1_dout), .WE(Reg_A), .Din(n8bit_register_1_dout),
    .Stored_data(Reg_A_DATA), .OE(OE_reg_A));
  _8bit_ALU u_8bit_alu_1 (
    .A(Reg_A_DATA), .B(Reg_B_DATA), .out_7(n8bit_register_1_dout), .out_8(ALU_RESULT), .SUB(SUB), .Cin(Cin),
    .SELECT(Select), .Cout(Cout), .OE(OE_ALU));  // open: Zero_Flag
  _8bit_register u_8bit_register_2 (
    .CLOCK(and_1_out), .WE(Reg_B), .Din(n8bit_register_1_dout), .Stored_data(Reg_B_DATA));  // open: DOut, OE
  Clock CLK_3 ();  // open: out
  Counter #(.width(4), .max('h6)) counter_1 (
    .load(LOAD), .D(controlled_buffer_1_out), .count(CE_COUNTER), .Q(COUNTER_DATA), .clk(and_1_out),
    .clr(RESET));  // open: carry
  Decinal_Decoder Decoder (.Din(Reg_A_DATA), .Dout({Decoder_dout_2, Decoder_dout}));
  Decinal_Decoder Decoder_2 (
    .Din(Reg_B_DATA),
    .Dout({Decoder_2_dout_4[31:28], Decoder_2_dout_7, Decoder_2_dout_6, Decoder_2_dout_5, Decoder_2_dout_4[15:12], Decoder_2_dout_3, Decoder_2_dout_2, Decoder_2_dout}));
  Clock CLK_4 ();  // open: out
  Clock CLK_5 ();  // open: out
  assign controlled_buffer_1_out = OE_PC ? COUNTER_DATA : 4'bz;  // Controlled_Buffer controlled_buffer_1
  assign bit_extender_1_out = {{4{1'b0}}, COUNTER_DATA};  // Bit_Extender bit_extender_1
  _8bit_register u_8bit_register_3 (
    .CLOCK(and_1_out), .DOut(n8bit_register_3_dout), .WE(WE_IR), .Din(n8bit_register_1_dout),
    .Stored_data(IR_DATA), .OE(OE_IR));
  _7_Segment_Display u_7_segment_display_1 (
    .g(Decoder_dout_2[11]), .f(Decoder_dout_2[10]), .a(Decoder_dout_2[9]), .b(Decoder_dout_2[8]),
    .e(Decoder_dout_2[27]), .d(Decoder_dout_2[26]), .c(Decoder_dout_2[25]), .dp(Decoder_dout_2[24]));
  _7_Segment_Display u_7_segment_display_2 (
    .g(Decoder_dout_2[15]), .f(Decoder_dout_2[14]), .a(Decoder_dout_2[13]), .b(Decoder_dout_2[12]),
    .e(Decoder_dout_2[31]), .d(Decoder_dout_2[30]), .c(Decoder_dout_2[29]), .dp(Decoder_dout_2[28]));
  _7_Segment_Display u_7_segment_display_3 (
    .g(Decoder_2_dout_4[15]), .f(Decoder_2_dout_4[14]), .a(Decoder_2_dout_4[13]), .b(Decoder_2_dout_4[12]),
    .e(Decoder_2_dout_4[31]), .d(Decoder_2_dout_4[30]), .c(Decoder_2_dout_4[29]), .dp(Decoder_2_dout_4[28]));
  Decinal_Decoder Decoder_3 (
    .Din(bit_extender_1_out),
    .Dout({Decoder_3_dout_5, Decoder_3_dout_4, Decoder_3_dout_3, Decoder_3_dout_2, Decoder_3_dout}));
  _7_Segment_Display u_7_segment_display_4 (
    .g(Decoder_dout[3]), .f(Decoder_dout[2]), .a(Decoder_dout[1]), .b(Decoder_dout[0]),
    .e(Decoder_dout_2[19]), .d(Decoder_dout_2[18]), .c(Decoder_dout_2[17]), .dp(Decoder_dout_2[16]));
  _7_Segment_Display u_7_segment_display_5 (
    .g(Decoder_dout_2[7]), .f(Decoder_dout_2[6]), .a(Decoder_dout_2[5]), .b(Decoder_dout_2[4]),
    .e(Decoder_dout_2[23]), .d(Decoder_dout_2[22]), .c(Decoder_dout_2[21]), .dp(Decoder_dout_2[20]));
  _7_Segment_Display u_7_segment_display_6 (
    .g(Decoder_2_dout_3[3]), .f(Decoder_2_dout_3[2]), .a(Decoder_2_dout_3[1]), .b(Decoder_2_dout_3[0]),
    .e(Decoder_2_dout_7[3]), .d(Decoder_2_dout_7[2]), .c(Decoder_2_dout_7[1]), .dp(Decoder_2_dout_7[0]));
  _7_Segment_Display u_7_segment_display_7 (
    .g(Decoder_2_dout_2[3]), .f(Decoder_2_dout_2[2]), .a(Decoder_2_dout_2[1]), .b(Decoder_2_dout_2[0]),
    .e(Decoder_2_dout_6[3]), .d(Decoder_2_dout_6[2]), .c(Decoder_2_dout_6[1]), .dp(Decoder_2_dout_6[0]));
  _7_Segment_Display u_7_segment_display_8 (
    .g(Decoder_3_dout[3]), .f(Decoder_3_dout[2]), .a(Decoder_3_dout[1]), .b(Decoder_3_dout[0]),
    .e(Decoder_3_dout_2[3]), .d(Decoder_3_dout_2[2]), .c(Decoder_3_dout_2[1]), .dp(Decoder_3_dout_2[0]));
  _7_Segment_Display u_7_segment_display_9 (
    .g(Decoder_2_dout[3]), .f(Decoder_2_dout[2]), .a(Decoder_2_dout[1]), .b(Decoder_2_dout[0]),
    .e(Decoder_2_dout_5[3]), .d(Decoder_2_dout_5[2]), .c(Decoder_2_dout_5[1]), .dp(Decoder_2_dout_5[0]));
  Clock CLK_6 ();  // open: out
  Clock CLK_7 ();  // open: out
  BitSelector #(.group(4)) bitselector_2 (.in(n8bit_register_3_dout), .out(controlled_buffer_1_out), .sel(1'b0));
  LED D6 (.in(n8bit_register_1_dout[6]));
  LED D5 (.in(n8bit_register_1_dout[5]));
  LED D7 (.in(n8bit_register_1_dout[7]));
  LED D4 (.in(n8bit_register_1_dout[4]));
  assign n8bit_register_1_dout = OE_2 ? test : 8'bz;  // Controlled_Buffer controlled_buffer_2
  LED D3 (.in(n8bit_register_1_dout[3]));
  LED D2 (.in(n8bit_register_1_dout[2]));
  Clock CLK_8 ();  // open: out
  Clock CLK_9 ();  // open: out
  LED D0 (.in(n8bit_register_1_dout[0]));
  LED D1 (.in(n8bit_register_1_dout[1]));
  assign n8bit_register_1_dout = INT_OE_MBR ? MBR_Data : 8'bz;  // Controlled_Buffer controlled_buffer_3
  _8bit_register MBR (
    .CLOCK(and_1_out), .DOut(n8bit_register_1_dout), .WE(WE_MBR), .Din(n8bit_register_1_dout),
    .Stored_data(MBR_Data), .OE(OE_MBR));
  _8bit_register Output_Reg (
    .CLOCK(and_1_out), .DOut(n8bit_register_1_dout), .WE(WE_OUT_REG), .Din(n8bit_register_1_dout),
    .Stored_data(out_64), .OE(OE_OUTPUT));
  MAR MAR (
    .Clock(and_1_out), .WE(WE_MAR), .Din(controlled_buffer_1_out), .OE(OE_MAR), .Stored_Data(MAR_Data),
    .Dout(MAR_dout));
  Decinal_Decoder Decoder_4 (.Din(out_64), .Dout(Decoder_4_dout));
  _7_Segment_Display u_7_segment_display_10 (
    .g(Decoder_4_dout[15]), .f(Decoder_4_dout[14]), .a(Decoder_4_dout[13]), .b(Decoder_4_dout[12]),
    .e(Decoder_4_dout[31]), .d(Decoder_4_dout[30]), .c(Decoder_4_dout[29]), .dp(Decoder_4_dout[28]));
  _7_Segment_Display u_7_segment_display_11 (
    .g(Decoder_4_dout[11]), .f(Decoder_4_dout[10]), .a(Decoder_4_dout[9]), .b(Decoder_4_dout[8]),
    .e(Decoder_4_dout[27]), .d(Decoder_4_dout[26]), .c(Decoder_4_dout[25]), .dp(Decoder_4_dout[24]));
  _7_Segment_Display u_7_segment_display_12 (
    .g(Decoder_4_dout[7]), .f(Decoder_4_dout[6]), .a(Decoder_4_dout[5]), .b(Decoder_4_dout[4]),
    .e(Decoder_4_dout[23]), .d(Decoder_4_dout[22]), .c(Decoder_4_dout[21]), .dp(Decoder_4_dout[20]));
  assign MAR_dout = OE ? in_2 : 4'bz;  // Controlled_Buffer controlled_buffer_4
  LED D7_2 (.in(n8bit_register_1_dout[7]));
  LED D6_2 (.in(n8bit_register_1_dout[6]));
  _7_Segment_Display u_7_segment_display_13 (
    .g(Decoder_4_dout[3]), .f(Decoder_4_dout[2]), .a(Decoder_4_dout[1]), .b(Decoder_4_dout[0]),
    .e(Decoder_4_dout[19]), .d(Decoder_4_dout[18]), .c(Decoder_4_dout[17]), .dp(Decoder_4_dout[16]));
  LED D3_2 (.in(n8bit_register_1_dout[3]));
  LED D4_2 (.in(n8bit_register_1_dout[4]));
  LED D2_2 (.in(n8bit_register_1_dout[2]));
  LED D5_2 (.in(n8bit_register_1_dout[5]));
  LED D1_2 (.in(n8bit_register_1_dout[1]));
  LED D0_2 (.in(n8bit_register_1_dout[0]));
  RAM #(.addrWidth(4), .bus("separate")) ram_1 (
    .addr(MAR_dout), .din(n8bit_register_1_dout), .data(n8bit_register_1_dout), .str(WE_RAM),
    .clk(and_1_out), .ld(OE_RAM));  // open: sel, clr

  assign CE = CE_COUNTER;
  assign COUNT_OE = OE_PC;
  assign IntOE = INT_OE_MBR;
  assign OE_3 = OE_RAM;
  assign OE_4 = OE_MAR;
  assign OE_5 = OE_IR;
  assign OE_6 = OE_MBR;
  assign OE_7 = OE_OUTPUT;
  assign OE_8 = OE_ALU;
  assign WE = WE_RAM;
  assign WE_2 = WE_MAR;
  assign WE_3 = WE_IR;
  assign WE_4 = WE_MBR;
  assign WE_5 = Reg_A;
  assign WE_6 = WE_OUT_REG;
  assign WE_7 = Reg_B;

  // Other names for the same wires on the sheet: IR_HALT[7:0] = IR_DATA

  // Notes on the sheet:
  //   MULT
  //   ADD
  //   SUB
  //   REG A
  //   REG B
  //   FETCH CYCLE
  //   LOAD A OR B
  //   STORE
  //   MOV B,A
  //   PC
  //   IR
  //   INTERNAL BUS (4 BIT)
  //   INTERNAL BUS
  //   EXTERNAL BUS (4BIT)
  //   EXTERNAL BUS
endmodule

module _8bit_ADDER (
  input  in_1,
  input  [7:0] in_2,
  input  [7:0] in_3,
  output out_4,
  output [7:0] out_5
);

  wire n1bit_adder_1_cout, n1bit_adder_2_cout, n1bit_adder_3_cout, n1bit_adder_4_cout, n1bit_adder_5_cout,
       n1bit_adder_6_cout, n1bit_adder_7_cout;

  _1bit_ADDER u_1bit_adder_1 (.A(in_2[0]), .B(in_3[0]), .SUM(out_5[0]), .Cout(n1bit_adder_1_cout), .Cin(in_1));
  _1bit_ADDER u_1bit_adder_2 (
    .A(in_2[1]), .B(in_3[1]), .SUM(out_5[1]), .Cout(n1bit_adder_2_cout), .Cin(n1bit_adder_1_cout));
  _1bit_ADDER u_1bit_adder_3 (
    .A(in_2[2]), .B(in_3[2]), .SUM(out_5[2]), .Cout(n1bit_adder_3_cout), .Cin(n1bit_adder_2_cout));
  _1bit_ADDER u_1bit_adder_4 (
    .A(in_2[3]), .B(in_3[3]), .SUM(out_5[3]), .Cout(n1bit_adder_4_cout), .Cin(n1bit_adder_3_cout));
  _1bit_ADDER u_1bit_adder_5 (
    .A(in_2[4]), .B(in_3[4]), .SUM(out_5[4]), .Cout(n1bit_adder_5_cout), .Cin(n1bit_adder_4_cout));
  _1bit_ADDER u_1bit_adder_6 (
    .A(in_2[5]), .B(in_3[5]), .SUM(out_5[5]), .Cout(n1bit_adder_6_cout), .Cin(n1bit_adder_5_cout));
  _1bit_ADDER u_1bit_adder_7 (
    .A(in_2[6]), .B(in_3[6]), .SUM(out_5[6]), .Cout(n1bit_adder_7_cout), .Cin(n1bit_adder_6_cout));
  _1bit_ADDER u_1bit_adder_8 (.A(in_2[7]), .B(in_3[7]), .SUM(out_5[7]), .Cout(out_4), .Cin(n1bit_adder_7_cout));
endmodule

module _1bit_ADDER (
  input  Cin,
  input  A,
  input  B,
  output SUM,
  output Cout
);

  wire and_1_out, and_2_out, xor_1_out;

  xor xor_1 (xor_1_out, A, B);
  and and_1 (and_1_out, A, B);
  xor xor_2 (SUM, xor_1_out, Cin);
  and and_2 (and_2_out, xor_1_out, Cin);
  or or_1 (Cout, and_2_out, and_1_out);
endmodule

module _1bit_ALU (
  input  A,
  input  B,
  input  Cin,
  input  [2:0] in_4,
  input  SUB,
  output out_6,
  output out_7
);

  wire and_1_out, n1bit_adder_1_sum, nor_1_out, or_1_out, xor_1_out, xor_2_out;

  xor xor_1 (xor_1_out, B, SUB);
  and and_1 (and_1_out, A, B);
  or or_1 (or_1_out, A, B);
  xor xor_2 (xor_2_out, A, B);
  nor nor_1 (nor_1_out, A, B);
  _1bit_ADDER u_1bit_adder_1 (.A(A), .B(xor_1_out), .SUM(n1bit_adder_1_sum), .Cout(out_7), .Cin(Cin));
  Multiplexer #(.select(3), .enable("false")) multiplexer_1 (
    .in0(and_1_out), .in1(or_1_out), .in2(xor_2_out), .in3(nor_1_out), .in4(n1bit_adder_1_sum), .out(out_6),
    .sel(in_4));  // open: in5, in6, in7
endmodule

module _8bit_ALU (
  input  [7:0] A,
  input  SUB,
  input  Cin,
  input  [2:0] SELECT,
  input  [7:0] B,
  input  OE,
  output [7:0] out_7,
  output [7:0] out_8,
  output Zero_Flag,
  output Cout
);

  wire n1bit_alu_1_out_7, n1bit_alu_2_out_7, n1bit_alu_3_out_7, n1bit_alu_4_out_7, n1bit_alu_5_out_7,
       n1bit_alu_6_out_7, n1bit_alu_7_out_7;
  wire [7:0] multiplier_1_out;

  Multiplier multiplier_1 (.a(A), .b(B), .out(multiplier_1_out));  // open: cin, cout
  _1bit_ALU u_1bit_alu_1 (
    .SUB(SUB), .out_6(out_8[0]), .out_7(n1bit_alu_1_out_7), .A(A[0]), .B(B[0]), .Cin(Cin), .in_4(SELECT));
  _1bit_ALU u_1bit_alu_2 (
    .SUB(SUB), .out_6(out_8[1]), .out_7(n1bit_alu_2_out_7), .A(A[1]), .B(B[1]), .Cin(n1bit_alu_1_out_7),
    .in_4(SELECT));
  _1bit_ALU u_1bit_alu_3 (
    .SUB(SUB), .out_6(out_8[2]), .out_7(n1bit_alu_3_out_7), .A(A[2]), .B(B[2]), .Cin(n1bit_alu_2_out_7),
    .in_4(SELECT));
  _1bit_ALU u_1bit_alu_4 (
    .SUB(SUB), .out_6(out_8[3]), .out_7(n1bit_alu_4_out_7), .A(A[3]), .B(B[3]), .Cin(n1bit_alu_3_out_7),
    .in_4(SELECT));
  _1bit_ALU u_1bit_alu_5 (
    .SUB(SUB), .out_6(out_8[4]), .out_7(n1bit_alu_5_out_7), .A(A[4]), .B(B[4]), .Cin(n1bit_alu_4_out_7),
    .in_4(SELECT));
  _1bit_ALU u_1bit_alu_6 (
    .SUB(SUB), .out_6(out_8[5]), .out_7(n1bit_alu_6_out_7), .A(A[5]), .B(B[5]), .Cin(n1bit_alu_5_out_7),
    .in_4(SELECT));
  _1bit_ALU u_1bit_alu_7 (
    .SUB(SUB), .out_6(out_8[6]), .out_7(n1bit_alu_7_out_7), .A(A[6]), .B(B[6]), .Cin(n1bit_alu_6_out_7),
    .in_4(SELECT));
  _1bit_ALU u_1bit_alu_8 (
    .SUB(SUB), .out_6(out_8[7]), .out_7(Cout), .A(A[7]), .B(B[7]), .Cin(n1bit_alu_7_out_7), .in_4(SELECT));
  Multiplexer #(.select(3), .width(8), .enable("false")) multiplexer_1 (
    .in5(multiplier_1_out), .out(out_8), .sel(SELECT));  // open: in0, in1, in2, in3, in4, in6, in7
  assign out_7 = OE ? out_8 : 8'bz;  // Controlled_Buffer controlled_buffer_1
  nor nor_1 (Zero_Flag, out_8[0], out_8[1], out_8[2], out_8[3], out_8[4], out_8[5], out_8[6], out_8[7]);
endmodule

module memory_cell (
  input  Clock,
  input  WE,
  input  Din,
  input  OE,
  input  Reset,
  output DOut,
  output Stored_DATA
);

  wire and_1_out, and_2_out, not_1_out, or_1_out;

  not not_1 (not_1_out, WE);
  and and_1 (and_1_out, Stored_DATA, not_1_out);
  and and_2 (and_2_out, WE, Din);
  or or_1 (or_1_out, and_1_out, and_2_out);
  D_Flip_Flop d_ff_1 (.clk(Clock), .D(or_1_out), .Q(Stored_DATA), .reset(Reset));  // open: Qn, preset, en
  assign DOut = OE ? Stored_DATA : 1'bz;  // Controlled_Buffer controlled_buffer_1
endmodule

module _8bit_register (
  input  CLOCK,
  input  WE,
  input  [7:0] Din,
  input  OE,
  output [7:0] DOut,
  output [7:0] Stored_data
);

  memory_cell memory_cell_1 (
    .WE(WE), .Din(Din[0]), .OE(OE), .DOut(DOut[0]), .Stored_DATA(Stored_data[0]), .Clock(CLOCK));  // open: Reset
  memory_cell memory_cell_2 (
    .WE(WE), .Din(Din[1]), .OE(OE), .DOut(DOut[1]), .Stored_DATA(Stored_data[1]), .Clock(CLOCK));  // open: Reset
  memory_cell memory_cell_3 (
    .WE(WE), .Din(Din[2]), .OE(OE), .DOut(DOut[2]), .Stored_DATA(Stored_data[2]), .Clock(CLOCK));  // open: Reset
  memory_cell memory_cell_4 (
    .WE(WE), .Din(Din[3]), .OE(OE), .DOut(DOut[3]), .Stored_DATA(Stored_data[3]), .Clock(CLOCK));  // open: Reset
  memory_cell memory_cell_5 (
    .WE(WE), .Din(Din[4]), .OE(OE), .DOut(DOut[4]), .Stored_DATA(Stored_data[4]), .Clock(CLOCK));  // open: Reset
  memory_cell memory_cell_6 (
    .WE(WE), .Din(Din[5]), .OE(OE), .DOut(DOut[5]), .Stored_DATA(Stored_data[5]), .Clock(CLOCK));  // open: Reset
  memory_cell memory_cell_7 (
    .WE(WE), .Din(Din[6]), .OE(OE), .DOut(DOut[6]), .Stored_DATA(Stored_data[6]), .Clock(CLOCK));  // open: Reset
  memory_cell memory_cell_8 (
    .WE(WE), .Din(Din[7]), .OE(OE), .DOut(DOut[7]), .Stored_DATA(Stored_data[7]), .Clock(CLOCK));  // open: Reset
endmodule

module Decinal_Decoder (
  input  [7:0] Din,
  output [31:0] Dout
);

  ROM #(.dataWidth(32)) rom_1 (
    .addr(Din),
    .data({Dout[31:28], Dout[15:12], Dout[27:24], Dout[11:8], Dout[23:20], Dout[7:4], Dout[19:16], Dout[3:0]}));  // open: sel
  _7_Segment_Display u_7_segment_display_1 (
    .g(Dout[11]), .f(Dout[10]), .a(Dout[9]), .b(Dout[8]), .e(Dout[27]), .d(Dout[26]), .c(Dout[25]),
    .dp(Dout[24]));
  _7_Segment_Display u_7_segment_display_2 (
    .g(Dout[15]), .f(Dout[14]), .a(Dout[13]), .b(Dout[12]), .e(Dout[31]), .d(Dout[30]), .c(Dout[29]),
    .dp(Dout[28]));
  _7_Segment_Display u_7_segment_display_3 (
    .g(Dout[3]), .f(Dout[2]), .a(Dout[1]), .b(Dout[0]), .e(Dout[19]), .d(Dout[18]), .c(Dout[17]),
    .dp(Dout[16]));
  _7_Segment_Display u_7_segment_display_4 (
    .g(Dout[7]), .f(Dout[6]), .a(Dout[5]), .b(Dout[4]), .e(Dout[23]), .d(Dout[22]), .c(Dout[21]),
    .dp(Dout[20]));

  // Notes on the sheet:
  //   contents of rom_1 (hex, n*v repeats v):
  //   e7 21 cb 6b 2d 6e ee 23 ef 2f 21e7 2121 21cb 216b 212d 216e 21ee 2123 21ef 212f cbe7 cb21 cbcb cb6b
  //   cb2d cb6e cbee cb23 cbef cb2f 6be7 6b21 6bcb 6b6b 6b2d 6b6e 6bee 6b23 6bef 6b2f 2de7 2d21 2dcb 2d6b
  //   2d2d 2d6e 2dee 2d23 2def 2d2f 6ee7 6e21 6ecb 6e6b 6e2d 6e6e 6eee 6e23 6eef 6e2f eee7 ee21 eecb ee6b
  //   ee2d ee6e eeee ee23 eeef ee2f 23e7 2321 23cb 236b 232d 236e 23ee 2323 23ef 232f efe7 ef21 efcb ef6b
  //   ef2d ef6e efee ef23 efef ef2f 2fe7 2f21 2fcb 2f6b 2f2d 2f6e 2fee 2f23 2fef 2f2f 21e7e7 21e721 21e7cb
  //   21e76b 21e72d 21e76e 21e7ee 21e723 21e7ef 21e72f 2121e7 212121 2121cb 21216b 21212d 21216e 2121ee
  //   212123 2121ef 21212f 21cbe7 21cb21 21cbcb 21cb6b 21cb2d 21cb6e 21cbee 21cb23 21cbef 21cb2f 216be7
  //   216b21 216bcb 216b6b 216b2d 216b6e 216bee 216b23 216bef 216b2f 212de7 212d21 212dcb 212d6b 212d2d
  //   212d6e 212dee 212d23 212def 212d2f 216ee7 216e21 216ecb 216e6b 216e2d 216e6e 216eee 216e23 216eef
  //   216e2f 21eee7 21ee21 21eecb 21ee6b 21ee2d 21ee6e 21eeee 21ee23 21eeef 21ee2f 2123e7 212321 2123cb
  //   21236b 21232d 21236e 2123ee 212323 2123ef 21232f 21efe7 21ef21 21efcb 21ef6b 21ef2d 21ef6e 21efee
  //   21ef23 21efef 21ef2f 212fe7 212f21 212fcb 212f6b 212f2d 212f6e 212fee 212f23 212fef 212f2f cbe7e7
  //   cbe721 cbe7cb cbe76b cbe72d cbe76e cbe7ee cbe723 cbe7ef cbe72f cb21e7 cb2121 cb21cb cb216b cb212d
  //   cb216e cb21ee cb2123 cb21ef cb212f cbcbe7 cbcb21 cbcbcb cbcb6b cbcb2d cbcb6e cbcbee cbcb23 cbcbef
  //   cbcb2f cb6be7 cb6b21 cb6bcb cb6b6b cb6b2d cb6b6e cb6bee cb6b23 cb6bef cb6b2f cb2de7 cb2d21 cb2dcb
  //   cb2d6b cb2d2d cb2d6e cb2dee cb2d23 cb2def cb2d2f cb6ee7 cb6e21 cb6ecb cb6e6b cb6e2d cb6e6e
endmodule

module BInaryto7seg (
  input  [15:0] in_1
);

  wire [13:0] bit_extender_1_out;
  wire [31:0] rom_1_data;

  Bit_Extender #(.in_width(16), .out_width(14)) bit_extender_1 (.in(in_1), .out(bit_extender_1_out));
  ROM #(.addrWidth(14), .dataWidth(32)) rom_1 (.addr(bit_extender_1_out), .data(rom_1_data));  // open: sel
  _7_Segment_Display u_7_segment_display_1 (
    .g(rom_1_data[27]), .f(rom_1_data[26]), .a(rom_1_data[25]), .b(rom_1_data[24]), .e(rom_1_data[31]),
    .d(rom_1_data[30]), .c(rom_1_data[29]), .dp(rom_1_data[28]));
  _7_Segment_Display u_7_segment_display_2 (
    .g(rom_1_data[19]), .f(rom_1_data[18]), .a(rom_1_data[17]), .b(rom_1_data[16]), .e(rom_1_data[23]),
    .d(rom_1_data[22]), .c(rom_1_data[21]), .dp(rom_1_data[20]));
  _7_Segment_Display u_7_segment_display_3 (
    .g(rom_1_data[11]), .f(rom_1_data[10]), .a(rom_1_data[9]), .b(rom_1_data[8]), .e(rom_1_data[15]),
    .d(rom_1_data[14]), .c(rom_1_data[13]), .dp(rom_1_data[12]));
  _7_Segment_Display u_7_segment_display_4 (
    .g(rom_1_data[3]), .f(rom_1_data[2]), .a(rom_1_data[1]), .b(rom_1_data[0]), .e(rom_1_data[7]),
    .d(rom_1_data[6]), .c(rom_1_data[5]), .dp(rom_1_data[4]));

  // Notes on the sheet:
  //   contents of rom_1 (hex, n*v repeats v):
  //   e7 21 cb 6b 2d 6e ee 23 ef 6f 21e7 2121 21cb 216b 212d 216e 21ee 2123 21ef 216f cbe7 cb21 cbcb cb6b
  //   cb2d cb6e cbee cb23 cbef cb6f 6be7 6b21 6bcb 6b6b 6b2d 6b6e 6bee 6b23 6bef 6b6f 2de7 2d21 2dcb 2d6b
  //   2d2d 2d6e 2dee 2d23 2def 2d6f 6ee7 6e21 6ecb 6e6b 6e2d 6e6e 6eee 6e23 6eef 6e6f eee7 ee21 eecb ee6b
  //   ee2d ee6e eeee ee23 eeef ee6f 23e7 2321 23cb 236b 232d 236e 23ee 2323 23ef 236f efe7 ef21 efcb ef6b
  //   ef2d ef6e efee ef23 efef ef6f 6fe7 6f21 6fcb 6f6b 6f2d 6f6e 6fee 6f23 6fef 6f6f 21e7e7 21e721 21e7cb
  //   21e76b 21e72d 21e76e 21e7ee 21e723 21e7ef 21e76f 2121e7 212121 2121cb 21216b 21212d 21216e 2121ee
  //   212123 2121ef 21216f 21cbe7 21cb21 21cbcb 21cb6b 21cb2d 21cb6e 21cbee 21cb23 21cbef 21cb6f 216be7
  //   216b21 216bcb 216b6b 216b2d 216b6e 216bee 216b23 216bef 216b6f 212de7 212d21 212dcb 212d6b 212d2d
  //   212d6e 212dee 212d23 212def 212d6f 216ee7 216e21 216ecb 216e6b 216e2d 216e6e 216eee 216e23 216eef
  //   216e6f 21eee7 21ee21 21eecb 21ee6b 21ee2d 21ee6e 21eeee 21ee23 21eeef 21ee6f 2123e7 212321 2123cb
  //   21236b 21232d 21236e 2123ee 212323 2123ef 21236f 21efe7 21ef21 21efcb 21ef6b 21ef2d 21ef6e 21efee
  //   21ef23 21efef 21ef6f 216fe7 216f21 216fcb 216f6b 216f2d 216f6e 216fee 216f23 216fef 216f6f cbe7e7
  //   cbe721 cbe7cb cbe76b cbe72d cbe76e cbe7ee cbe723 cbe7ef cbe76f cb21e7 cb2121 cb21cb cb216b cb212d
  //   cb216e cb21ee cb2123 cb21ef cb216f cbcbe7 cbcb21 cbcbcb cbcb6b cbcb2d cbcb6e cbcbee cbcb23 cbcbef
  //   cbcb6f cb6be7 cb6b21 cb6bcb cb6b6b cb6b2d cb6b6e cb6bee cb6b23 cb6bef cb6b6f cb2de7 cb2d21 cb2dcb
  //   cb2d6b cb2d2d cb2d6e cb2dee cb2d23 cb2def cb2d6f cb6ee7 cb6e21 cb6ecb cb6e6b cb6e2d cb6e6e cb6eee
  //   cb6e23 cb6eef cb6e6f cbeee7 cbee21 cbeecb cbee6b cbee2d cbee6e cbeeee cbee23 cbeeef cbee6f cb23e7
  //   cb2321 cb23cb cb236b cb232d cb236e cb23ee cb2323 cb23ef cb236f cbefe7 cbef21 cbefcb cbef6b cbef2d
  //   cbef6e cbefee cbef23 cbefef cbef6f cb6fe7 cb6f21 cb6fcb cb6f6b cb6f2d cb6f6e cb6fee cb6f23 cb6fef
  //   cb6f6f 6be7e7 6be721 6be7cb 6be76b 6be72d 6be76e 6be7ee 6be723 6be7ef 6be76f 6b21e7 6b2121 6b21cb
  //   6b216b 6b212d 6b216e 6b21ee 6b2123 6b21ef 6b216f 6bcbe7 6bcb21 6bcbcb 6bcb6b 6bcb2d 6bcb6e 6bcbee
  //   6bcb23 6bcbef 6bcb6f 6b6be7 6b6b21 6b6bcb 6b6b6b 6b6b2d 6b6b6e 6b6bee 6b6b23 6b6bef 6b6b6f 6b2de7
  //   6b2d21 6b2dcb 6b2d6b 6b2d2d 6b2d6e 6b2dee 6b2d23 6b2def 6b2d6f 6b6ee7 6b6e21 6b6ecb 6b6e6b 6b6e2d
  //   6b6e6e 6b6eee 6b6e23 6b6eef 6b6e6f 6beee7 6bee21 6beecb 6bee6b 6bee2d 6bee6e 6beeee 6bee23 6beeef
  //   6bee6f 6b23e7 6b2321 6b23cb 6b236b 6b232d 6b236e 6b23ee 6b2323 6b23ef 6b236f 6befe7 6bef21 6befcb
  //   6bef6b 6bef2d 6bef6e 6befee 6bef23 6befef 6bef6f 6b6fe7 6b6f21 6b6fcb 6b6f6b 6b6f2d 6b6f6e 6b6fee
  //   6b6f23 6b6fef 6b6f6f 2de7e7 2de721 2de7cb 2de76b 2de72d 2de76e 2de7ee 2de723 2de7ef 2de76f 2d21e7
  //   2d2121 2d21cb 2d216b 2d212d 2d216e 2d21ee 2d2123 2d21ef 2d216f 2dcbe7 2dcb21 2dcbcb 2dcb6b 2dcb2d
  //   2dcb6e 2dcbee 2dcb23 2dcbef 2dcb6f 2d6be7 2d6b21 2d6bcb 2d6b6b 2d6b2d 2d6b6e 2d6bee 2d6b23 2d6bef
  //   2d6b6f 2d2de7 2d2d21 2d2dcb 2d2d6b 2d2d2d 2d2d6e 2d2dee 2d2d23 2d2def 2d2d6f 2d6ee7 2d6e21 2d6ecb
  //   2d6e6b 2d6e2d 2d6e6e 2d6eee 2d6e23 2d6eef 2d6e6f 2deee7 2dee21 2deecb 2dee6b 2dee2d 2dee6e 2deeee
  //   2dee23 2deeef 2dee6f 2d23e7 2d2321 2d23cb 2d236b 2d232d 2d236e 2d23ee 2d2323 2d23ef 2d236f 2defe7
  //   2def21 2defcb 2def6b 2def2d 2def6e 2defee 2def23 2defef 2def6f 2d6fe7 2d6f21 2d6fcb 2d6f6b 2d6f2d
  //   2d6f6e 2d6fee 2d6f23 2d6fef 2d6f6f 6ee7e7 6ee721 6ee7cb 6ee76b 6ee72d 6ee76e 6ee7ee 6ee723 6ee7ef
  //   6ee76f 6e21e7 6e2121 6e21cb 6e216b 6e212d 6e216e 6e21ee 6e2123 6e21ef 6e216f 6ecbe7 6ecb21 6ecbcb
  //   6ecb6b 6ecb2d 6ecb6e 6ecbee 6ecb23 6ecbef 6ecb6f 6e6be7 6e6b21 6e6bcb 6e6b6b 6e6b2d 6e6b6e 6e6bee
  //   6e6b23 6e6bef 6e6b6f 6e2de7 6e2d21 6e2dcb 6e2d6b 6e2d2d 6e2d6e 6e2dee 6e2d23 6e2def 6e2d6f 6e6ee7
  //   6e6e21 6e6ecb 6e6e6b 6e6e2d 6e6e6e 6e6eee 6e6e23 6e6eef 6e6e6f 6eeee7 6eee21 6eeecb 6eee6b 6eee2d
  //   6eee6e 6eeeee 6eee23 6eeeef 6eee6f 6e23e7 6e2321 6e23cb 6e236b 6e232d 6e236e 6e23ee 6e2323 6e23ef
  //   6e236f 6eefe7 6eef21 6eefcb 6eef6b 6eef2d 6eef6e 6eefee 6eef23 6eefef 6eef6f 6e6fe7 6e6f21 6e6fcb
  //   6e6f6b 6e6f2d 6e6f6e 6e6fee 6e6f23 6e6fef 6e6f6f eee7e7 eee721 eee7cb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
endmodule

module MAR (
  input  Clock,
  input  WE,
  input  [3:0] Din,
  input  OE,
  output [3:0] Dout,
  output [3:0] Stored_Data
);

  memory_cell memory_cell_1 (
    .WE(WE), .Din(Din[0]), .OE(OE), .DOut(Dout[0]), .Stored_DATA(Stored_Data[0]), .Clock(Clock));  // open: Reset
  memory_cell memory_cell_2 (
    .WE(WE), .Din(Din[1]), .OE(OE), .DOut(Dout[1]), .Stored_DATA(Stored_Data[1]), .Clock(Clock));  // open: Reset
  memory_cell memory_cell_3 (
    .WE(WE), .Din(Din[2]), .OE(OE), .DOut(Dout[2]), .Stored_DATA(Stored_Data[2]), .Clock(Clock));  // open: Reset
  memory_cell memory_cell_4 (
    .WE(WE), .Din(Din[3]), .OE(OE), .DOut(Dout[3]), .Stored_DATA(Stored_Data[3]), .Clock(Clock));  // open: Reset
endmodule
